# Fritzing sketch SondeAlarm (saved by Fritzing 0.9.2b)
breadboards: 1

parts:
  U1 = LCD-16X2 [package=lcd-16x2]
  Composant1 = Arduino Nano (Rev3.0)
  Pot1 = Trimmer Potentiometer [maximum_resistance=10kΩ package=THT]
  R1 = Resistor [tolerance=±5% resistance=220 package=THT]
  R2 = Resistor [tolerance=±5% resistance=4.7k package=THT]
  Pot2 = Trimmer Potentiometer [maximum_resistance=10kΩ package=THT]

nets:
  VSS: U1.VSS, U1.R_W, U1.K, Composant1.GND, Pot1.leg1, Pot1.leg2, Pot2.leg1
  VDD: U1.VDD, Composant1.5V, R1.Pin_1, R2.Pin_1, Pot2.leg2
  N1: U1.VO, Pot1.wiper
  N2: U1.RS, Composant1.D12/MISO
  N3: U1.E, Composant1.D11/MOSI
  N4: U1.DB4, Composant1.D7
  N5: U1.DB5, Composant1.D6
  N6: U1.DB6, Composant1.D5
  N7: U1.DB7, Composant1.D4
  N8: U1.A, R1.Pin_0
  N9: Composant1.D9, R2.Pin_0
  N10: Composant1.A2, Pot2.wiper

notes:
  Volume Alarme (?)
  Réglage contraste LCD
  Sonde DS18B20
